# Fritzing sketch Schema_pendolo (saved by Fritzing 0.9.4)

parts:
  Componente1 = Arduino Uno (Rev3)
  hc-sr1 = hc-sr04

nets:
  N1: Componente1.D2, hc-sr1.Trig
  N2: Componente1.D4, hc-sr1.Echo
  5V: Componente1.5V, hc-sr1.VCC
  GND: Componente1.GND, hc-sr1.GND
